// Logisim project ejGuia.circ as structural Verilog: 10 circuits, main circuit main
module main (
  input  c1,
  input  c2,
  input  e0,
  output s0,
  output s1,
  output s2,
  output s3
);

  wire and_1_out, and_2_out, and_3_out, nor_1_out, not_1_out, not_2_out;

  not not_1 (not_1_out, c1);
  and and_1 (and_1_out, c2, not_1_out);
  not not_2 (not_2_out, c2);
  nor nor_1 (nor_1_out, c2, c1);
  and and_2 (and_2_out, not_2_out, c1);
  and and_3 (and_3_out, c2, c1);
  and and_4 (s0, nor_1_out, e0);
  and and_5 (s1, and_1_out, e0);
  and and_6 (s2, and_2_out, e0);
  and and_7 (s3, and_3_out, e0);
endmodule

module ej9 (
  input  e0,
  input  e1,
  input  e2,
  input  e3,
  output s0,
  output s1,
  output out_7
);

  wire and_1_out, and_2_out, and_3_out, and_4_out, not_1_out, not_2_out, not_3_out, not_4_out, xor_1_out,
       xor_2_out;

  not not_1 (not_1_out, e2);
  not not_2 (not_2_out, e3);
  not not_3 (not_3_out, e1);
  not not_4 (not_4_out, e0);
  and and_1 (and_1_out, not_1_out, not_2_out);
  xor xor_1 (xor_1_out, e0, e1);
  and and_2 (and_2_out, not_3_out, not_4_out);
  xor xor_2 (xor_2_out, e2, e3);
  and and_3 (and_3_out, and_1_out, xor_1_out);
  and and_4 (and_4_out, and_2_out, xor_2_out);
  or or_1 (s0, e1, e3);
  or or_2 (s1, e2, e3);
  or or_3 (out_7, and_3_out, and_4_out);
endmodule

module ej10 (
  input  e0,
  input  e1,
  output s0,
  output s1,
  output s2,
  output s3
);

  wire not_1_out, not_2_out, not_3_out, not_4_out;

  not not_1 (not_1_out, e0);
  not not_2 (not_2_out, e1);
  not not_3 (not_3_out, e1);
  not not_4 (not_4_out, e0);
  and and_1 (s0, not_1_out, not_2_out);
  and and_2 (s1, e0, not_3_out);
  and and_3 (s2, not_4_out, e1);
  and and_4 (s3, e1, e0);
endmodule

module ej10b (
  input  e0,
  input  c0,
  input  c1,
  output s0,
  output s1,
  output s3,
  output s4
);

  wire ej10_1_s0, ej10_1_s1, ej10_1_s2, ej10_1_s3;

  ej10 ej10_1 (.e0(c0), .e1(c1), .s0(ej10_1_s0), .s1(ej10_1_s1), .s2(ej10_1_s2), .s3(ej10_1_s3));
  and and_1 (s0, ej10_1_s0, e0);
  and and_2 (s1, ej10_1_s1, e0);
  and and_3 (s3, ej10_1_s2, e0);
  and and_4 (s4, ej10_1_s3, e0);
endmodule

module ej14 (
  input  i0,
  input  i1,
  input  i2,
  input  i3,
  input  load,
  input  clk,
  output o0,
  output o1,
  output o2,
  output o3
);

  wire multiplexer_1_out, multiplexer_2_out, multiplexer_3_out, multiplexer_4_out;

  D_Flip_Flop d_ff_1 (.D(multiplexer_1_out), .clk(clk), .Q(o0));  // open: Qn, preset, reset
  Multiplexer multiplexer_1 (.in0(o0), .in1(i0), .out(multiplexer_1_out), .sel(load));
  Multiplexer multiplexer_2 (.in0(o1), .in1(i1), .out(multiplexer_2_out), .sel(load));
  D_Flip_Flop d_ff_2 (.D(multiplexer_2_out), .clk(clk), .Q(o1));  // open: Qn, preset, reset
  Multiplexer multiplexer_3 (.in0(o2), .in1(i2), .out(multiplexer_3_out), .sel(load));
  D_Flip_Flop d_ff_3 (.D(multiplexer_3_out), .clk(clk), .Q(o2));  // open: Qn, preset, reset
  D_Flip_Flop d_ff_4 (.D(multiplexer_4_out), .clk(clk), .Q(o3));  // open: Qn, preset, reset
  Multiplexer multiplexer_4 (.in0(o3), .in1(i3), .out(multiplexer_4_out), .sel(load));
endmodule

module ej15 (
  input  d3,
  input  d2,
  input  d1,
  input  d0,
  input  load,
  input  clk,
  input  read,
  output d3_out,
  output d2_out,
  output d1_out,
  output d0_out
);

  wire d_ff_1_q, d_ff_2_q, d_ff_3_q, d_ff_4_q, multiplexer_1_out, multiplexer_2_out, multiplexer_3_out,
       multiplexer_4_out;

  D_Flip_Flop d_ff_1 (.D(multiplexer_1_out), .clk(clk), .Q(d_ff_1_q));  // open: Qn, preset, reset
  Multiplexer multiplexer_1 (.in0(d_ff_1_q), .in1(d3), .out(multiplexer_1_out), .sel(load));
  assign d3_out = read ? d_ff_1_q : 1'bz;  // Controlled_Buffer controlled_buffer_1
  D_Flip_Flop d_ff_2 (.D(multiplexer_2_out), .clk(clk), .Q(d_ff_2_q));  // open: Qn, preset, reset
  Multiplexer multiplexer_2 (.in0(d_ff_2_q), .in1(d2), .out(multiplexer_2_out), .sel(load));
  assign d2_out = read ? d_ff_2_q : 1'bz;  // Controlled_Buffer controlled_buffer_2
  D_Flip_Flop d_ff_3 (.D(multiplexer_3_out), .clk(clk), .Q(d_ff_3_q));  // open: Qn, preset, reset
  assign d1_out = read ? d_ff_3_q : 1'bz;  // Controlled_Buffer controlled_buffer_3
  Multiplexer multiplexer_3 (.in0(d_ff_3_q), .in1(d1), .out(multiplexer_3_out), .sel(load));
  Multiplexer multiplexer_4 (.in0(d_ff_4_q), .in1(d0), .out(multiplexer_4_out), .sel(load));
  D_Flip_Flop d_ff_4 (.D(multiplexer_4_out), .clk(clk), .Q(d_ff_4_q));  // open: Qn, preset, reset
  assign d0_out = read ? d_ff_4_q : 1'bz;  // Controlled_Buffer controlled_buffer_4
endmodule

module ej16 (
  input  i0,
  input  i1,
  input  i2,
  input  i3,
  input  load,
  input  clk,
  input  ext,
  output o0,
  output o1,
  output o2,
  output o3
);

  wire ej14_1_o2, ej14_1_o3;

  ej14 ej14_1 (
    .i0(i0), .i1(i1), .i2(i2), .i3(i3), .load(load), .clk(clk), .o0(o0), .o1(o1), .o2(ej14_1_o2),
    .o3(ej14_1_o3));
  Multiplexer multiplexer_1 (.in0(ej14_1_o2), .in1(o1), .out(o2), .sel(ext));
  Multiplexer multiplexer_2 (.in0(ej14_1_o3), .in1(o1), .out(o3), .sel(ext));
endmodule

module ej17 (
  input  i0,
  input  i1,
  input  i2,
  input  i3,
  input  load,
  input  clk,
  input  shl,
  output o0,
  output o1,
  output o2,
  output o3
);

  wire ej14_1_o0, ej14_1_o1, ej14_1_o2, ej14_1_o3;

  ej14 ej14_1 (
    .i0(i0), .i1(i1), .i2(i2), .i3(i3), .load(load), .clk(clk), .o0(ej14_1_o0), .o1(ej14_1_o1),
    .o2(ej14_1_o2), .o3(ej14_1_o3));
  Multiplexer multiplexer_1 (.in0(ej14_1_o0), .in1(ej14_1_o1), .out(o0), .sel(shl));
  Multiplexer multiplexer_2 (.in0(ej14_1_o1), .in1(ej14_1_o2), .out(o1), .sel(shl));
  Multiplexer multiplexer_3 (.in0(ej14_1_o2), .in1(ej14_1_o3), .out(o2), .sel(shl));
  Multiplexer multiplexer_4 (.in0(ej14_1_o3), .in1(ej14_1_o0), .out(o3), .sel(shl));
endmodule

module ej18 (
  input  d3,
  input  d2,
  input  d1,
  input  d0,
  input  load,
  input  clk,
  input  read,
  input  inc,
  output d3_out,
  output d2_out,
  output d1_out,
  output d0_out
);

  wire d_ff_1_q, d_ff_2_q, d_ff_3_q, d_ff_4_q, incrementador_1_s0, incrementador_1_s1, incrementador_1_s2,
       incrementador_1_s3, multiplexer_1_out, multiplexer_2_out, multiplexer_3_out, multiplexer_4_out,
       multiplexer_5_out, multiplexer_6_out, multiplexer_7_out, multiplexer_8_out;

  D_Flip_Flop d_ff_1 (.D(multiplexer_1_out), .clk(clk), .Q(d_ff_1_q));  // open: Qn, preset, reset
  Multiplexer multiplexer_1 (.in0(multiplexer_8_out), .in1(d3), .out(multiplexer_1_out), .sel(load));
  assign d3_out = read ? d_ff_1_q : 1'bz;  // Controlled_Buffer controlled_buffer_1
  D_Flip_Flop d_ff_2 (.D(multiplexer_2_out), .clk(clk), .Q(d_ff_2_q));  // open: Qn, preset, reset
  Multiplexer multiplexer_2 (.in0(multiplexer_7_out), .in1(d2), .out(multiplexer_2_out), .sel(load));
  assign d2_out = read ? d_ff_2_q : 1'bz;  // Controlled_Buffer controlled_buffer_2
  D_Flip_Flop d_ff_3 (.D(multiplexer_3_out), .clk(clk), .Q(d_ff_3_q));  // open: Qn, preset, reset
  Multiplexer multiplexer_3 (.in0(multiplexer_6_out), .in1(d1), .out(multiplexer_3_out), .sel(load));
  assign d1_out = read ? d_ff_3_q : 1'bz;  // Controlled_Buffer controlled_buffer_3
  Multiplexer multiplexer_4 (.in0(multiplexer_5_out), .in1(d0), .out(multiplexer_4_out), .sel(load));
  D_Flip_Flop d_ff_4 (.D(multiplexer_4_out), .clk(clk), .Q(d_ff_4_q));  // open: Qn, preset, reset
  assign d0_out = read ? d_ff_4_q : 1'bz;  // Controlled_Buffer controlled_buffer_4
  incrementador incrementador_1 (
    .e0(d_ff_4_q), .e1(d_ff_3_q), .e2(d_ff_2_q), .e3(d_ff_1_q), .s0(incrementador_1_s0),
    .s1(incrementador_1_s1), .s2(incrementador_1_s2), .s3(incrementador_1_s3));
  Multiplexer multiplexer_5 (.in0(d_ff_4_q), .in1(incrementador_1_s0), .out(multiplexer_5_out), .sel(inc));
  Multiplexer multiplexer_6 (.in0(d_ff_3_q), .in1(incrementador_1_s1), .out(multiplexer_6_out), .sel(inc));
  Multiplexer multiplexer_7 (.in0(d_ff_2_q), .in1(incrementador_1_s2), .out(multiplexer_7_out), .sel(inc));
  Multiplexer multiplexer_8 (.in0(d_ff_1_q), .in1(incrementador_1_s3), .out(multiplexer_8_out), .sel(inc));
endmodule

module incrementador (
  input  e0,
  input  e1,
  input  e2,
  input  e3,
  output s0,
  output s1,
  output s2,
  output s3
);

  wire and_1_out, and_2_out;

  not not_1 (s0, e0);
  and and_1 (and_1_out, e0, e1);
  xor xor_1 (s1, e0, e1);
  xor xor_2 (s2, and_1_out, e2);
  and and_2 (and_2_out, and_1_out, e2);
  xor xor_3 (s3, and_2_out, e3);
endmodule
