// Logisim project taller3.circ as structural Verilog: 9 circuits, main circuit main
module main (
  input  pulsador,
  input  reset,
  output o1,
  output o0
);

  wire and_1_out, d_ff_2_qn;

  D_Flip_Flop d_ff_1 (.D(d_ff_2_qn), .clk(pulsador), .Q(o1), .reset(reset));  // open: Qn, preset
  and and_1 (and_1_out, d_ff_2_qn, o1);
  D_Flip_Flop d_ff_2 (.D(and_1_out), .clk(pulsador), .Q(o0), .Qn(d_ff_2_qn), .preset(reset));  // open: reset
endmodule

module contador2b (
  input  pulsador,
  output o0,
  output o1
);

  J_K_Flip_Flop j_k_ff_1 (.J(1'b1), .K(1'b1), .clk(pulsador), .Q(o0));  // open: Qn, preset, reset
  J_K_Flip_Flop j_k_ff_2 (.J(o0), .K(o0), .clk(pulsador), .Q(o1));  // open: Qn, preset, reset
endmodule

module ej3 (
  input  pulsador,
  output o0,
  output o1
);

  wire contador2b_1_o0, contador2b_1_o1, not_1_out;

  contador2b contador2b_1 (.pulsador(pulsador), .o0(contador2b_1_o0), .o1(contador2b_1_o1));
  not not_1 (not_1_out, contador2b_1_o0);
  or or_1 (o0, contador2b_1_o0, contador2b_1_o1);
  and and_1 (o1, not_1_out, contador2b_1_o1);
endmodule

module ej3bis (
  input  NEG,
  input  pulsador,
  output o0,
  output o1
);

  wire ej3_1_o0, ej3_1_o1;

  ej3 ej3_1 (.pulsador(pulsador), .o0(ej3_1_o0), .o1(ej3_1_o1));
  xor xor_1 (o0, NEG, ej3_1_o0);
  xor xor_2 (o1, NEG, ej3_1_o1);
endmodule

module ejB1 (
  input  pulsador,
  input  reset,
  output o1,
  output o0
);

  wire main_1_o0, main_1_o1;

  main main_1 (.pulsador(pulsador), .reset(reset), .o1(main_1_o1), .o0(main_1_o0));
  traductor traductor_1 (.q1(main_1_o1), .q0(main_1_o0), .o1(o1), .o0(o0));
endmodule

module traductor (
  input  q1,
  input  q0,
  output o1,
  output o0
);

  wire xor_1_out;

  xor xor_1 (xor_1_out, q0, q1);
  not not_1 (o1, q1);
  not not_2 (o0, xor_1_out);
endmodule

module ejB3 (
  input  pulsador,
  output o1,
  output o0
);

  wire ej3_1_o0, ej3_1_o1;

  ej3 ej3_1 (.pulsador(pulsador), .o0(ej3_1_o0), .o1(ej3_1_o1));
  traductor traductor_1 (.q1(ej3_1_o1), .q0(ej3_1_o0), .o1(o1), .o0(o0));
endmodule

module ejB3bis (
  input  NEG,
  input  pulsador,
  output o1,
  output o0
);

  wire ejb3_1_o0, ejb3_1_o1;

  ejB3 ejb3_1 (.pulsador(pulsador), .o1(ejb3_1_o1), .o0(ejb3_1_o0));
  xor xor_1 (o1, NEG, ejb3_1_o1);
  xor xor_2 (o0, NEG, ejb3_1_o0);
endmodule

module ejB3bis_v2 (
  input  NEG,
  input  pulsador,
  output o1,
  output o0
);

  wire ej3bis_1_o0, ej3bis_1_o1;

  ej3bis ej3bis_1 (.NEG(NEG), .pulsador(pulsador), .o0(ej3bis_1_o0), .o1(ej3bis_1_o1));
  traductor traductor_1 (.q1(ej3bis_1_o1), .q0(ej3bis_1_o0), .o1(o1), .o0(o0));
endmodule
